# Fritzing sketch SmartBriefBox (saved by Fritzing 0.9.3b)
breadboards: 1

parts:
  元件1 = Arduino Nano (Rev3.0)
  VCC1 = 4 x AAA Battery Mount
  U1 = ESP8266 WiFi Module [part_number=ESP8266]
  GY1 = MPU-6050 Board GY-521 [form="♀ (female)" package=THT]
  IC1 = Voltage Regulator [package=to-220-alt]
  C1 = Tantalum Capacitor [capacitance=2.2µF package="100 mil [THT, tantalum]"]
  C2 = Tantalum Capacitor [capacitance=2.2µF package="100 mil [THT, tantalum]"]
  R1 = Resistor [tolerance=±5% resistance=470 package=THT]
  R2 = Resistor [tolerance=±5% resistance=10k package=THT]
  D1 = Zener Diode [part_number=1N4732A breakdown_voltage=3.6V package="300 mil [THT]"]
  R3 = Resistor [tolerance=±5% resistance=470 package=THT]

nets:
  GND: 元件1.GND, VCC1.-, U1.GND, GY1.pin2, IC1.GND, C1.-, C2.-
  N1: 元件1.D2, R1.Pin_0
  N2: 元件1.D6, D1.cathode, R3.Pin_0
  N3: 元件1.5V, VCC1.+, GY1.pin1, IC1.IN, C2.+
  N4: 元件1.A5, GY1.pin3
  N5: 元件1.A4, GY1.pin4
  N6: U1.VCC, IC1.OUT, C1.+, R2.Pin_0, R3.Pin_1
  N7: U1.RST, D1.anode
  N8: U1.CH_PD, R2.Pin_1
  N9: GY1.pin8, R1.Pin_1

custom parts:
  ESP8266 WiFi Module: Generic WiFi Module based on the ESP8266 with onboard PCB antenna and UART communications
  MPU-6050 Board GY-521: Acelerometro y Giroscopio MPU-6050 Board GY-521
